// Logisim project CombinationalLogic.circ as structural Verilog: 5 circuits, main circuit main
module main (
  input  in_1,
  input  in_2,
  input  in_3,
  input  [3:0] in_4,
  input  [3:0] in_5,
  input  \_4_2编码器 ,
  input  in_7,
  input  in_8,
  input  in_9,
  input  \_4_2优先编码器 ,
  input  in_11,
  input  in_12,
  input  in_13,
  input  \_4_2优先编码器2 ,
  input  in_15,
  input  in_16,
  input  in_17,
  output out_18,
  output out_19,
  output out_20,
  output out_21,
  output out_22,
  output out_23,
  output out_24,
  output out_25,
  output out_26,
  output out_27,
  output l,
  output h,
  output out_30,
  output out_31
);

  wire and_2_out, and_3_out, and_4_out, and_5_out, and_6_out, and_7_out, and_8_out, and_9_out, and_10_out,
       and_11_out, and_12_out, and_13_out, decoder2_4_1_out_3, decoder2_4_1_out_4, decoder2_4_1_out_5,
       decoder2_4_1_out_6, decoder2_4_2_out_3, decoder2_4_2_out_4, decoder2_4_2_out_5, decoder2_4_2_out_6,
       decoder2_4_3_out_3, decoder2_4_3_out_4, decoder2_4_3_out_5, decoder2_4_3_out_6, decoder2_4_4_out_3,
       decoder2_4_4_out_4, decoder2_4_4_out_5, decoder2_4_4_out_6, decoder_1_out0, decoder_1_out1,
       decoder_1_out2, decoder_1_out3, decoder_1_out4, decoder_1_out5, decoder_1_out6, decoder_1_out7,
       decoder_1_out8, decoder_1_out9, decoder_1_out10, decoder_1_out11, decoder_1_out12, decoder_1_out13,
       decoder_1_out14, decoder_1_out15, decoder_2_out0, decoder_2_out1, decoder_2_out2, decoder_2_out3,
       decoder_2_out4, decoder_2_out5, decoder_2_out6, decoder_2_out7, decoder_2_out8, decoder_2_out9,
       decoder_2_out10, decoder_2_out11, decoder_2_out12, decoder_2_out13, decoder_2_out14, decoder_2_out15,
       dipswitch_1_p1, dipswitch_1_p2, dipswitch_1_p3, dipswitch_1_p4, dipswitch_1_p5, dipswitch_1_p6,
       dipswitch_1_p7, dipswitch_1_p8, dipswitch_1_p9, dipswitch_1_p10, dipswitch_1_p11, dipswitch_1_p12,
       dipswitch_1_p13, dipswitch_1_p14, dipswitch_1_p15, dipswitch_1_p16, not_1_out, not_2_out, not_3_out,
       not_4_out, not_5_out, not_6_out, not_7_out, not_8_out, not_9_out, not_10_out, not_11_out, not_12_out,
       or_1_out, or_6_out, or_7_out, or_8_out, or_9_out, or_10_out, or_11_out, or_12_out, or_17_out,
       or_18_out, or_19_out, or_20_out, or_21_out, or_22_out, or_23_out, seven_segment_circuit16_1_a,
       seven_segment_circuit16_1_b, seven_segment_circuit16_1_c, seven_segment_circuit16_1_d,
       seven_segment_circuit16_1_e, seven_segment_circuit16_1_f, seven_segment_circuit16_1_g;
  wire [3:0] low1_out;

  // DipSwitch #(.number(16)) dipswitch_1: pin names not known; wires that end beside it: dipswitch_1_p1, dipswitch_1_p2, dipswitch_1_p3, dipswitch_1_p4, dipswitch_1_p5, dipswitch_1_p6, dipswitch_1_p7, dipswitch_1_p8, dipswitch_1_p9, dipswitch_1_p10, dipswitch_1_p11, dipswitch_1_p12, dipswitch_1_p13, dipswitch_1_p14, dipswitch_1_p15, dipswitch_1_p16
  not not_1 (not_1_out, in_1);
  not not_2 (not_2_out, in_2);
  not not_3 (not_3_out, in_3);
  Decoder #(.enable("false"), .select(4)) decoder_1 (
    .out0(decoder_1_out0), .out1(decoder_1_out1), .out2(decoder_1_out2), .out3(decoder_1_out3),
    .out4(decoder_1_out4), .out5(decoder_1_out5), .out6(decoder_1_out6), .out7(decoder_1_out7),
    .out8(decoder_1_out8), .out9(decoder_1_out9), .out10(decoder_1_out10), .out11(decoder_1_out11),
    .out12(decoder_1_out12), .out13(decoder_1_out13), .out14(decoder_1_out14), .out15(decoder_1_out15),
    .sel(in_4));
  or low1 (low1_out[0], dipswitch_1_p2, dipswitch_1_p4, dipswitch_1_p6, dipswitch_1_p8, dipswitch_1_p10, dipswitch_1_p12, dipswitch_1_p14, dipswitch_1_p16);
  or or_1 (or_1_out, decoder_1_out15, decoder_1_out14, decoder_1_out13, decoder_1_out12, decoder_1_out11, decoder_1_out10);
  or or_2 (low1_out[1], dipswitch_1_p3, dipswitch_1_p4, dipswitch_1_p7, dipswitch_1_p8, dipswitch_1_p11, dipswitch_1_p12, dipswitch_1_p15, dipswitch_1_p16);
  or or_3 (low1_out[2], dipswitch_1_p5, dipswitch_1_p6, dipswitch_1_p7, dipswitch_1_p8, dipswitch_1_p13, dipswitch_1_p14, dipswitch_1_p15, dipswitch_1_p16);
  or high1 (low1_out[3], dipswitch_1_p9, dipswitch_1_p10, dipswitch_1_p11, dipswitch_1_p12, dipswitch_1_p13, dipswitch_1_p14, dipswitch_1_p15, dipswitch_1_p16);
  or or_4 (out_26, in_7, in_9);
  or or_5 (out_27, in_8, in_9);
  decoder2_4 decoder2_4_1 (
    .in_1(in_1), .in_2(not_2_out), .out_3(decoder2_4_1_out_3), .out_4(decoder2_4_1_out_4),
    .out_5(decoder2_4_1_out_5), .out_6(decoder2_4_1_out_6));
  decoder2_4 decoder2_4_2 (
    .in_1(not_1_out), .in_2(in_2), .out_3(decoder2_4_2_out_3), .out_4(decoder2_4_2_out_4),
    .out_5(decoder2_4_2_out_5), .out_6(decoder2_4_2_out_6));
  decoder2_4 decoder2_4_3 (
    .in_1(in_2), .in_2(in_3), .out_3(decoder2_4_3_out_3), .out_4(decoder2_4_3_out_4),
    .out_5(decoder2_4_3_out_5), .out_6(decoder2_4_3_out_6));
  decoder2_4 decoder2_4_4 (
    .in_1(not_2_out), .in_2(not_3_out), .out_3(decoder2_4_4_out_3), .out_4(decoder2_4_4_out_4),
    .out_5(decoder2_4_4_out_5), .out_6(decoder2_4_4_out_6));
  _7_Segment_Display u_7_segment_display_1 (
    .g(seven_segment_circuit16_1_g), .f(seven_segment_circuit16_1_f), .a(seven_segment_circuit16_1_a),
    .b(seven_segment_circuit16_1_b), .e(seven_segment_circuit16_1_e), .d(seven_segment_circuit16_1_d),
    .c(seven_segment_circuit16_1_c));  // open: dp
  not not_4 (not_4_out, in_11);
  // AND_Gate and_1 has open pins: in0=\_4_2优先编码器 , in1=not_4_out, in2=not_5_out, in3=not_6_out, out=open
  not not_5 (not_5_out, in_12);
  not not_6 (not_6_out, in_13);
  not not_7 (not_7_out, in_12);
  and and_2 (and_2_out, in_11, not_7_out, not_8_out);
  not not_8 (not_8_out, in_13);
  and and_3 (and_3_out, in_12, not_9_out);
  not not_9 (not_9_out, in_13);
  not not_10 (not_10_out, in_16);
  and and_4 (and_4_out, in_15, not_10_out, not_11_out);
  not not_11 (not_11_out, in_17);
  and and_5 (and_5_out, in_16, not_12_out);
  not not_12 (not_12_out, in_17);
  and and_6 (and_6_out, decoder2_4_1_out_3, decoder2_4_2_out_6);
  and and_7 (and_7_out, decoder2_4_1_out_4, decoder2_4_2_out_5);
  and and_8 (and_8_out, decoder2_4_1_out_6, decoder2_4_2_out_3);
  and and_9 (and_9_out, decoder2_4_1_out_5, decoder2_4_2_out_4);
  and and_10 (and_10_out, decoder2_4_3_out_4, decoder2_4_4_out_5);
  and and_11 (and_11_out, decoder2_4_3_out_3, decoder2_4_4_out_6);
  and and_12 (and_12_out, decoder2_4_3_out_5, decoder2_4_4_out_4);
  and and_13 (and_13_out, decoder2_4_3_out_6, decoder2_4_4_out_3);
  seven_segment_circuit16 seven_segment_circuit16_1 (
    .in_1(low1_out), .a(seven_segment_circuit16_1_a), .b(seven_segment_circuit16_1_b),
    .c(seven_segment_circuit16_1_c), .d(seven_segment_circuit16_1_d), .e(seven_segment_circuit16_1_e),
    .f(seven_segment_circuit16_1_f), .g(seven_segment_circuit16_1_g));
  or or_6 (or_6_out, decoder_1_out0, decoder_1_out2, decoder_1_out3, decoder_1_out9, decoder_1_out5, decoder_1_out6, decoder_1_out7, decoder_1_out8);
  or or_7 (or_7_out, decoder_1_out0, decoder_1_out1, decoder_1_out2, decoder_1_out3, decoder_1_out4, decoder_1_out8, decoder_1_out7, decoder_1_out9);
  or or_8 (or_8_out, decoder_1_out0, decoder_1_out1, decoder_1_out3, decoder_1_out4, decoder_1_out5, decoder_1_out6, decoder_1_out7, decoder_1_out8, decoder_1_out9);
  or or_9 (or_9_out, decoder_1_out0, decoder_1_out2, decoder_1_out3, decoder_1_out5, decoder_1_out6, decoder_1_out8, decoder_1_out9);
  or or_10 (or_10_out, decoder_1_out0, decoder_1_out2, decoder_1_out6, decoder_1_out8);
  or or_11 (or_11_out, decoder_1_out0, decoder_1_out4, decoder_1_out5, decoder_1_out6, decoder_1_out8, decoder_1_out9);
  or or_12 (or_12_out, decoder_1_out2, decoder_1_out3, decoder_1_out4, decoder_1_out5, decoder_1_out6, decoder_1_out8, decoder_1_out9);
  or or_13 (l, in_13, and_2_out);
  or or_14 (h, and_3_out, in_13);
  or or_15 (out_30, in_17, and_4_out);
  or or_16 (out_31, and_5_out, in_17);
  and and_14 (out_18, and_7_out, and_11_out);
  and and_15 (out_19, and_7_out, and_10_out);
  and and_16 (out_20, and_6_out, and_12_out);
  and and_17 (out_21, and_6_out, and_13_out);
  and and_18 (out_22, and_11_out, and_8_out);
  and and_19 (out_23, and_8_out, and_10_out);
  buf and_20 (out_24, and_12_out);  // AND_Gate
  and and_21 (out_25, and_9_out, and_13_out);
  _7_Segment_Display u_7_segment_display_2 (
    .g(or_12_out), .f(or_11_out), .a(or_6_out), .b(or_7_out), .e(or_10_out), .d(or_9_out), .c(or_8_out),
    .dp(or_1_out));
  Decoder #(.enable("false"), .select(4)) decoder_2 (
    .out0(decoder_2_out0), .out1(decoder_2_out1), .out2(decoder_2_out2), .out3(decoder_2_out3),
    .out4(decoder_2_out4), .out5(decoder_2_out5), .out6(decoder_2_out6), .out7(decoder_2_out7),
    .out8(decoder_2_out8), .out9(decoder_2_out9), .out10(decoder_2_out10), .out11(decoder_2_out11),
    .out12(decoder_2_out12), .out13(decoder_2_out13), .out14(decoder_2_out14), .out15(decoder_2_out15),
    .sel(in_5));
  or or_17 (or_17_out, decoder_2_out10, decoder_2_out12, decoder_2_out0, decoder_2_out2, decoder_2_out3, decoder_2_out9, decoder_2_out5, decoder_2_out6, decoder_2_out7, decoder_2_out8, decoder_2_out14, decoder_2_out15);
  or or_18 (or_18_out, decoder_2_out10, decoder_2_out0, decoder_2_out1, decoder_2_out2, decoder_2_out3, decoder_2_out4, decoder_2_out8, decoder_2_out7, decoder_2_out9, decoder_2_out13);
  or or_19 (or_19_out, decoder_2_out5, decoder_2_out10, decoder_2_out0, decoder_2_out1, decoder_2_out3, decoder_2_out4, decoder_2_out6, decoder_2_out7, decoder_2_out8, decoder_2_out9, decoder_2_out11, decoder_2_out13);
  or or_20 (or_20_out, decoder_2_out11, decoder_2_out12, decoder_2_out0, decoder_2_out2, decoder_2_out3, decoder_2_out5, decoder_2_out6, decoder_2_out8, decoder_2_out9, decoder_2_out13, decoder_2_out14);
  or or_21 (or_21_out, decoder_2_out10, decoder_2_out11, decoder_2_out12, decoder_2_out0, decoder_2_out2, decoder_2_out6, decoder_2_out8, decoder_2_out13, decoder_2_out14, decoder_2_out15);
  or or_22 (or_22_out, decoder_2_out10, decoder_2_out11, decoder_2_out0, decoder_2_out4, decoder_2_out5, decoder_2_out12, decoder_2_out6, decoder_2_out8, decoder_2_out9, decoder_2_out14, decoder_2_out15);
  or or_23 (or_23_out, decoder_2_out5, decoder_2_out10, decoder_2_out11, decoder_2_out2, decoder_2_out3, decoder_2_out4, decoder_2_out6, decoder_2_out8, decoder_2_out9, decoder_2_out13, decoder_2_out14, decoder_2_out15);
  _7_Segment_Display u_7_segment_display_3 (
    .g(or_23_out), .f(or_22_out), .a(or_17_out), .b(or_18_out), .e(or_21_out), .d(or_20_out), .c(or_19_out));  // open: dp

  // Notes on the sheet:
  //   七段数码管译码器1
  //   2-4译码器实现3-8译码器
  //   16-4编码器
  //   七段数码管译码器2
endmodule

module decoder2_4 (
  input  in_1,
  input  in_2,
  output out_3,
  output out_4,
  output out_5,
  output out_6
);

  wire not_1_out, not_2_out;

  not not_1 (not_1_out, in_1);
  not not_2 (not_2_out, in_2);
  and and_1 (out_3, not_1_out, not_2_out);
  and and_2 (out_4, not_1_out, in_2);
  and and_3 (out_5, in_1, not_2_out);
  and and_4 (out_6, in_1, in_2);

  // Notes on the sheet:
  //   2-4译码器
endmodule

module seven_segment_circuit16 (
  input  [3:0] in_1,
  output a,
  output b,
  output c,
  output d,
  output e,
  output f,
  output g
);

  wire decoder_1_out0, decoder_1_out1, decoder_1_out2, decoder_1_out3, decoder_1_out4, decoder_1_out5,
       decoder_1_out6, decoder_1_out7, decoder_1_out8, decoder_1_out9, decoder_1_out10, decoder_1_out11,
       decoder_1_out12, decoder_1_out13, decoder_1_out14, decoder_1_out15;

  Decoder #(.enable("false"), .select(4)) decoder_1 (
    .out0(decoder_1_out0), .out1(decoder_1_out1), .out2(decoder_1_out2), .out3(decoder_1_out3),
    .out4(decoder_1_out4), .out5(decoder_1_out5), .out6(decoder_1_out6), .out7(decoder_1_out7),
    .out8(decoder_1_out8), .out9(decoder_1_out9), .out10(decoder_1_out10), .out11(decoder_1_out11),
    .out12(decoder_1_out12), .out13(decoder_1_out13), .out14(decoder_1_out14), .out15(decoder_1_out15),
    .sel(in_1));
  or or_1 (a, decoder_1_out10, decoder_1_out12, decoder_1_out0, decoder_1_out2, decoder_1_out3, decoder_1_out9, decoder_1_out5, decoder_1_out6, decoder_1_out7, decoder_1_out8, decoder_1_out14, decoder_1_out15);
  or or_2 (b, decoder_1_out10, decoder_1_out0, decoder_1_out1, decoder_1_out2, decoder_1_out3, decoder_1_out4, decoder_1_out8, decoder_1_out7, decoder_1_out9, decoder_1_out13);
  or or_3 (c, decoder_1_out5, decoder_1_out10, decoder_1_out0, decoder_1_out1, decoder_1_out3, decoder_1_out4, decoder_1_out6, decoder_1_out7, decoder_1_out8, decoder_1_out9, decoder_1_out11, decoder_1_out13);
  or or_4 (d, decoder_1_out11, decoder_1_out12, decoder_1_out0, decoder_1_out2, decoder_1_out3, decoder_1_out5, decoder_1_out6, decoder_1_out8, decoder_1_out9, decoder_1_out13, decoder_1_out14);
  or or_5 (e, decoder_1_out10, decoder_1_out11, decoder_1_out12, decoder_1_out0, decoder_1_out2, decoder_1_out6, decoder_1_out8, decoder_1_out13, decoder_1_out14, decoder_1_out15);
  or or_6 (f, decoder_1_out10, decoder_1_out11, decoder_1_out0, decoder_1_out4, decoder_1_out5, decoder_1_out12, decoder_1_out6, decoder_1_out8, decoder_1_out9, decoder_1_out14, decoder_1_out15);
  or or_7 (g, decoder_1_out5, decoder_1_out10, decoder_1_out11, decoder_1_out2, decoder_1_out3, decoder_1_out4, decoder_1_out6, decoder_1_out8, decoder_1_out9, decoder_1_out13, decoder_1_out14, decoder_1_out15);

  // Notes on the sheet:
  //   七段数码管译码器2
endmodule

module encoder16_4 (
  input  in_1,
  input  in_2,
  input  in_3,
  input  in_4,
  input  in_5,
  input  in_6,
  input  in_7,
  input  in_8,
  input  in_9,
  input  in_10,
  input  in_11,
  input  in_12,
  input  in_13,
  input  in_14,
  input  in_15,
  input  in_16,
  output out_17,
  output out_18,
  output out_19,
  output out_20
);

  or low1 (out_17, in_2, in_4, in_6, in_8, in_10, in_12, in_14, in_16);
  or or_1 (out_18, in_3, in_4, in_7, in_8, in_11, in_12, in_15, in_16);
  or or_2 (out_19, in_5, in_6, in_7, in_8, in_13, in_14, in_15, in_16);
  or high1 (out_20, in_9, in_10, in_11, in_12, in_13, in_14, in_15, in_16);
endmodule

module priority_encoder4_2 (
  input  \_4_2优先编码器 ,
  input  in_2,
  input  in_3,
  input  in_4,
  output out_5,
  output out_6
);

  wire and_1_out, and_2_out, not_1_out, not_2_out, not_3_out;

  not not_1 (not_1_out, in_3);
  not not_2 (not_2_out, in_4);
  not not_3 (not_3_out, in_4);
  and and_1 (and_1_out, in_2, not_1_out, not_2_out);
  and and_2 (and_2_out, in_3, not_3_out);
  or or_1 (out_5, in_4, and_1_out);
  or or_2 (out_6, and_2_out, in_4);
endmodule
