// Logisim project SequentialLogic.circ as structural Verilog: 2 circuits, main circuit main
module main (
  output out_1,
  output out_2,
  output Q,
  output nQ,
  output Q_2,
  output out_6,
  output Q_3,
  output out_8,
  output out_9
);

  wire and_1_out, and_2_out, and_3_out, and_4_out, and_5_out, and_6_out, and_7_out, and_8_out, and_9_out,
       and_10_out, and_11_out, and_12_out, dipswitch_1_p1, dipswitch_2_p1, dipswitch_3_p1, dipswitch_4_p1,
       dipswitch_5_p1, dipswitch_10_p1, dipswitch_11_p1, dipswitch_12_p1, dipswitch_13_p1, not_1_out,
       not_2_out, not_3_out, not_4_out, not_5_out, not_6_out, or_1_out, or_2_out, sr_latch_3_q;

  // DipSwitch #(.number(1)) dipswitch_1: pin names not known; wires that end beside it: dipswitch_1_p1
  // DipSwitch #(.number(1)) dipswitch_2: pin names not known; wires that end beside it: dipswitch_2_p1
  // DipSwitch #(.number(1)) dipswitch_3: pin names not known; wires that end beside it: dipswitch_3_p1
  // DipSwitch #(.number(1)) dipswitch_4: pin names not known; wires that end beside it: dipswitch_4_p1
  not not_1 (not_1_out, dipswitch_1_p1);
  // DipSwitch #(.number(1)) dipswitch_5: pin names not known; wires that end beside it: dipswitch_5_p1
  // DipSwitch #(.number(1)) dipswitch_6: pin names not known
  buf and_1 (and_1_out, dipswitch_2_p1);  // AND_Gate
  buf and_2 (and_2_out, dipswitch_2_p1);  // AND_Gate
  // DipSwitch #(.number(1)) dipswitch_7: pin names not known
  // DipSwitch #(.number(1)) dipswitch_8: pin names not known
  buf and_3 (and_3_out, dipswitch_3_p1);  // AND_Gate
  buf and_4 (and_4_out, dipswitch_3_p1);  // AND_Gate
  // DipSwitch #(.number(1)) dipswitch_9: pin names not known
  not not_2 (not_2_out, dipswitch_10_p1);
  // DipSwitch #(.number(1)) dipswitch_10: pin names not known; wires that end beside it: dipswitch_10_p1
  not not_3 (not_3_out, dipswitch_11_p1);
  // DipSwitch #(.number(1)) dipswitch_11: pin names not known; wires that end beside it: dipswitch_11_p1
  and and_5 (and_5_out, dipswitch_1_p1, dipswitch_4_p1);
  and and_6 (and_6_out, dipswitch_4_p1, not_1_out);
  and and_7 (and_7_out, dipswitch_5_p1, not_2_out);
  // DipSwitch #(.number(1)) dipswitch_12: pin names not known; wires that end beside it: dipswitch_12_p1
  or or_1 (or_1_out, dipswitch_10_p1, not_4_out);
  not not_4 (not_4_out, dipswitch_5_p1);
  and and_8 (and_8_out, not_6_out, not_3_out);
  // DipSwitch #(.number(1)) dipswitch_13: pin names not known; wires that end beside it: dipswitch_13_p1
  or or_2 (or_2_out, dipswitch_11_p1, not_5_out);
  not not_5 (not_5_out, not_6_out);
  nor nor_1 (out_1, and_1_out, out_2);
  nor nor_2 (out_2, out_1, and_2_out);
  nand nand_1 (Q, and_3_out, nQ);
  nand nand_2 (nQ, Q, and_4_out);
  and and_9 (and_9_out, and_7_out, dipswitch_12_p1);
  and and_10 (and_10_out, dipswitch_12_p1, or_1_out);
  and and_11 (and_11_out, and_8_out, dipswitch_13_p1);
  and and_12 (and_12_out, dipswitch_13_p1, or_2_out);
  SR_Latch sr_latch_1 (.R(and_6_out), .S(and_5_out), .Q(Q_2), .NQ(out_6));
  SR_Latch sr_latch_2 (.R(and_10_out), .S(and_9_out), .Q(Q_3), .NQ(out_8));
  not not_6 (not_6_out, sr_latch_3_q);
  SR_Latch sr_latch_3 (.R(and_12_out), .S(and_11_out), .Q(sr_latch_3_q), .NQ(out_9));

  // Notes on the sheet:
  //   D锁存器
  //   D
  //   SR锁存器
  //   ~S~R锁存器
  //   R
  //   S
  //   WE
  //   带复位的D锁存器
  //   R
  //   D
  //   D锁存器实现位翻转功能
  //   R
  //   D
  //   WE
  //   WE
  //   ~Q
  //   ~Q
  //   Q
  //   ~Q
endmodule

module SR_Latch (
  input  R,
  input  S,
  output Q,
  output NQ
);

  nor nor_1 (Q, R, NQ);
  nor nor_2 (NQ, Q, S);

  // Notes on the sheet:
  //   SR锁存器
endmodule
